// Logisim project 1bit_comparator.circ as structural Verilog: 10 circuits, main circuit Onebit
module Onebit (
  input  A,
  input  B,
  output B_A,
  output out_4,
  output A_B
);

  wire not_1_out, not_2_out, or_1_out;

  not not_1 (not_1_out, A);
  not not_2 (not_2_out, B);
  and and_1 (B_A, not_1_out, B);
  and and_2 (A_B, A, not_2_out);
  or or_1 (or_1_out, B_A, A_B);
  not not_3 (out_4, or_1_out);

  // Notes on the sheet:
  //   A=B
endmodule

module fourbit_comparator (
  input  A0,
  input  B0,
  input  A1,
  input  B1,
  input  A2,
  input  B2,
  input  A3,
  input  B3,
  output B,
  output A,
  output E
);

  wire and_1_out, and_2_out, and_3_out, and_4_out, and_5_out, and_6_out, onebit_1_a_b, onebit_1_b_a,
       onebit_1_out_4, onebit_2_a_b, onebit_2_b_a, onebit_2_out_4, onebit_3_a_b, onebit_3_b_a,
       onebit_3_out_4, onebit_4_a_b, onebit_4_b_a, onebit_4_out_4;

  Onebit onebit_1 (.A_B(onebit_1_a_b), .B_A(onebit_1_b_a), .A(A0), .B(B0), .out_4(onebit_1_out_4));
  Onebit onebit_2 (.A_B(onebit_2_a_b), .B_A(onebit_2_b_a), .A(A1), .B(B1), .out_4(onebit_2_out_4));
  Onebit onebit_3 (.A_B(onebit_3_a_b), .B_A(onebit_3_b_a), .A(A2), .B(B2), .out_4(onebit_3_out_4));
  Onebit onebit_4 (.A_B(onebit_4_a_b), .B_A(onebit_4_b_a), .A(A3), .B(B3), .out_4(onebit_4_out_4));
  and and_1 (and_1_out, onebit_1_out_4, onebit_2_b_a);
  and and_2 (and_2_out, onebit_1_out_4, onebit_2_a_b);
  and and_3 (and_3_out, onebit_1_out_4, onebit_2_out_4, onebit_3_b_a);
  and and_4 (and_4_out, onebit_1_out_4, onebit_2_out_4, onebit_3_a_b);
  and and_5 (and_5_out, onebit_1_out_4, onebit_2_out_4, onebit_3_out_4, onebit_4_b_a);
  and and_6 (and_6_out, onebit_1_out_4, onebit_2_out_4, onebit_3_out_4, onebit_4_a_b);
  and and_7 (E, onebit_1_out_4, onebit_2_out_4, onebit_3_out_4, onebit_4_out_4);
  or or_1 (B, onebit_1_b_a, and_1_out, and_3_out, and_5_out);
  or or_2 (A, onebit_1_a_b, and_2_out, and_4_out, and_6_out);

  // Notes on the sheet:
  //   A=B
  //   B>A
  //   A>B
endmodule

module eight_bit (
  input  A0,
  input  B0,
  input  A1,
  input  B1,
  input  A2,
  input  B2,
  input  A3,
  input  B3,
  input  A4,
  input  B4,
  input  A5,
  input  B5,
  input  A6,
  input  B6,
  input  A7,
  input  B7,
  output B,
  output A,
  output E
);

  wire and_1_out, and_2_out, fourbit_comparator_1_a, fourbit_comparator_1_b, fourbit_comparator_1_e,
       fourbit_comparator_2_a, fourbit_comparator_2_b, fourbit_comparator_2_e;

  fourbit_comparator fourbit_comparator_1 (
    .B(fourbit_comparator_1_b), .A2(A2), .B1(B1), .B3(B3), .B2(B2), .B0(B0), .A3(A3),
    .A(fourbit_comparator_1_a), .E(fourbit_comparator_1_e), .A0(A0), .A1(A1));
  fourbit_comparator fourbit_comparator_2 (
    .B(fourbit_comparator_2_b), .A2(A6), .B1(B5), .B3(B7), .B2(B6), .B0(B4), .A3(A7),
    .A(fourbit_comparator_2_a), .E(fourbit_comparator_2_e), .A0(A4), .A1(A5));
  and and_1 (and_1_out, fourbit_comparator_1_e, fourbit_comparator_2_b);
  and and_2 (and_2_out, fourbit_comparator_1_e, fourbit_comparator_2_a);
  or or_1 (B, fourbit_comparator_1_b, and_1_out);
  or or_2 (A, fourbit_comparator_1_a, and_2_out);
  and and_3 (E, fourbit_comparator_1_e, fourbit_comparator_2_e);
  fourbit_comparator fourbit_comparator_3 ();  // open: B, A2, B1, B3, B2, B0, A3, A, E, A0, A1

  // Notes on the sheet:
  //   MSB
  //   MSB
  //   B>A
  //   A>B
  //   A=B
endmodule

module c2eightbits (
  input  [7:0] Ain,
  input  [7:0] Bin,
  output B,
  output A,
  output E
);

  wire eight_bit_1_a, eight_bit_1_b, xorpropio_1_out_3;

  eight_bit eight_bit_1 (
    .A0(Ain[7]), .B0(Bin[7]), .A1(Ain[6]), .B1(Bin[6]), .A2(Ain[5]), .B2(Bin[5]), .A3(Ain[4]), .B3(Bin[4]),
    .A4(Ain[3]), .B4(Bin[3]), .A5(Ain[2]), .B5(Bin[2]), .A6(Ain[1]), .B6(Bin[1]), .A7(Ain[0]), .B7(Bin[0]),
    .B(eight_bit_1_b), .A(eight_bit_1_a), .E(E));
  XorPropio xorpropio_1 (.in_1(Ain[7]), .in_2(Bin[7]), .out_3(xorpropio_1_out_3));
  XorPropio xorpropio_2 (.in_1(xorpropio_1_out_3), .in_2(eight_bit_1_b), .out_3(B));
  XorPropio xorpropio_3 (.in_1(eight_bit_1_a), .in_2(xorpropio_1_out_3), .out_3(A));

  // Notes on the sheet:
  //   A=B
  //   B>A
  //   A>B
endmodule

module XorPropio (
  input  in_1,
  input  in_2,
  output out_3
);

  wire and_1_out, not_1_out, or_1_out;

  and and_1 (and_1_out, in_1, in_2);
  not not_1 (not_1_out, and_1_out);
  or or_1 (or_1_out, in_2, in_1);
  and and_2 (out_3, not_1_out, or_1_out);
endmodule

module TwonumberSort (
  input  [7:0] in_1,
  input  [7:0] in_2,
  output [7:0] Menor,
  output Igual,
  output [7:0] Mayor
);

  wire c2eightbits_1_a;

  // Probe on in_1
  // Probe on in_2
  c2eightbits c2eightbits_1 (.Ain(in_1), .Bin(in_2), .A(c2eightbits_1_a), .E(Igual));  // open: B
  // Probe on Menor
  // Probe on Mayor
  MuxPropio muxpropio_1 (.in_1(in_1), .in_2(in_2), .in_3(c2eightbits_1_a), .out_4(Mayor));
  MuxPropio muxpropio_2 (.in_1(in_2), .in_2(in_1), .in_3(c2eightbits_1_a), .out_4(Menor));
endmodule

module MuxPropio (
  input  [7:0] in_1,
  input  [7:0] in_2,
  input  in_3,
  output [7:0] out_4
);

  wire [7:0] and_1_out, and_2_out, bit_extender_1_out, not_1_out;

  assign bit_extender_1_out = {{7{in_3}}, in_3};  // Bit_Extender bit_extender_1
  assign not_1_out = ~bit_extender_1_out;  // NOT_Gate not_1, 8 bits wide
  assign and_1_out = in_2 & not_1_out;  // AND_Gate and_1, 8 bits wide
  assign and_2_out = in_1 & bit_extender_1_out;  // AND_Gate and_2, 8 bits wide
  assign out_4 = and_1_out | and_2_out;  // OR_Gate or_1, 8 bits wide
endmodule

module FournumberSort (
  input  [7:0] in_1,
  input  [7:0] in_2,
  input  [7:0] in_3,
  input  [7:0] in_4,
  output [7:0] Menor,
  output [7:0] SegundoMenor,
  output [7:0] SegundoMayor,
  output [7:0] Mayor,
  output Igual
);

  wire twonumbersort_1_igual, twonumbersort_2_igual, twonumbersort_3_igual, twonumbersort_5_igual;
  wire [7:0] twonumbersort_1_mayor, twonumbersort_1_menor, twonumbersort_2_mayor, twonumbersort_2_menor,
       twonumbersort_3_mayor, twonumbersort_4_menor;

  // Probe on in_1
  // Probe on in_2
  // Probe on in_3
  // Probe on in_4
  TwonumberSort twonumbersort_1 (
    .in_1(in_1), .in_2(in_2), .Menor(twonumbersort_1_menor), .Igual(twonumbersort_1_igual),
    .Mayor(twonumbersort_1_mayor));
  TwonumberSort twonumbersort_2 (
    .in_1(in_3), .in_2(in_4), .Menor(twonumbersort_2_menor), .Igual(twonumbersort_2_igual),
    .Mayor(twonumbersort_2_mayor));
  and and_1 (Igual, twonumbersort_2_igual, twonumbersort_1_igual, twonumbersort_3_igual, twonumbersort_5_igual);
  TwonumberSort twonumbersort_3 (
    .in_1(twonumbersort_1_menor), .in_2(twonumbersort_2_menor), .Menor(Menor), .Igual(twonumbersort_3_igual),
    .Mayor(twonumbersort_3_mayor));
  TwonumberSort twonumbersort_4 (
    .in_1(twonumbersort_1_mayor), .in_2(twonumbersort_2_mayor), .Menor(twonumbersort_4_menor), .Mayor(Mayor));  // open: Igual
  // Probe on SegundoMenor
  // Probe on SegundoMayor
  // Probe on Mayor
  // Probe on Menor
  TwonumberSort twonumbersort_5 (
    .in_1(twonumbersort_3_mayor), .in_2(twonumbersort_4_menor), .Menor(SegundoMenor),
    .Igual(twonumbersort_5_igual), .Mayor(SegundoMayor));
endmodule

module EightnumberSort (
  input  [7:0] in_1,
  input  [7:0] in_2,
  input  [7:0] in_3,
  input  [7:0] in_4,
  input  [7:0] in_5,
  input  [7:0] in_6,
  input  [7:0] in_7,
  input  [7:0] in_8,
  output [7:0] De_menor,
  output [7:0] out_10,
  output [7:0] out_11,
  output [7:0] out_12,
  output [7:0] out_13,
  output [7:0] out_14,
  output [7:0] out_15,
  output [7:0] A_mayor,
  output Igual
);

  wire fournumbersort_1_igual, fournumbersort_2_igual, fournumbersort_3_igual, fournumbersort_4_igual;
  wire [7:0] fournumbersort_1_mayor, fournumbersort_1_menor, fournumbersort_1_segundomayor,
       fournumbersort_1_segundomenor, fournumbersort_2_mayor, fournumbersort_2_menor,
       fournumbersort_2_segundomayor, fournumbersort_2_segundomenor, fournumbersort_3_mayor,
       fournumbersort_3_segundomayor, fournumbersort_4_menor, fournumbersort_4_segundomenor;

  // Probe on in_1
  // Probe on in_1
  // Probe on in_4
  // Probe on in_3
  // Probe on in_5
  // Probe on in_6
  // Probe on in_2
  // Probe on in_8
  // Probe on in_7
  FournumberSort fournumbersort_1 (
    .in_1(in_1), .in_2(in_2), .in_3(in_3), .in_4(in_4), .Menor(fournumbersort_1_menor),
    .SegundoMenor(fournumbersort_1_segundomenor), .SegundoMayor(fournumbersort_1_segundomayor),
    .Mayor(fournumbersort_1_mayor), .Igual(fournumbersort_1_igual));
  FournumberSort fournumbersort_2 (
    .in_1(in_5), .in_2(in_6), .in_3(in_7), .in_4(in_8), .Menor(fournumbersort_2_menor),
    .SegundoMenor(fournumbersort_2_segundomenor), .SegundoMayor(fournumbersort_2_segundomayor),
    .Mayor(fournumbersort_2_mayor), .Igual(fournumbersort_2_igual));
  and and_1 (Igual, fournumbersort_2_igual, fournumbersort_1_igual, fournumbersort_4_igual, fournumbersort_3_igual);
  FournumberSort fournumbersort_3 (
    .in_1(fournumbersort_1_menor), .in_2(fournumbersort_1_segundomenor), .in_3(fournumbersort_2_menor),
    .in_4(fournumbersort_2_segundomenor), .Menor(De_menor), .SegundoMenor(out_10),
    .SegundoMayor(fournumbersort_3_segundomayor), .Mayor(fournumbersort_3_mayor),
    .Igual(fournumbersort_3_igual));
  FournumberSort fournumbersort_4 (
    .in_1(fournumbersort_1_mayor), .in_2(fournumbersort_1_segundomayor),
    .in_3(fournumbersort_2_segundomayor), .in_4(fournumbersort_2_mayor), .Menor(fournumbersort_4_menor),
    .SegundoMenor(fournumbersort_4_segundomenor), .SegundoMayor(out_15), .Mayor(A_mayor),
    .Igual(fournumbersort_4_igual));
  FournumberSort fournumbersort_5 (
    .in_1(fournumbersort_3_segundomayor), .in_2(fournumbersort_3_mayor), .in_3(fournumbersort_4_menor),
    .in_4(fournumbersort_4_segundomenor), .Menor(out_11), .SegundoMenor(out_12), .SegundoMayor(out_13),
    .Mayor(out_14));  // open: Igual
  // Probe on De_menor
  // Probe on out_10
  // Probe on out_11
  // Probe on out_12
  // Probe on out_13
  // Probe on out_14
  // Probe on out_15
  // Probe on A_mayor
endmodule

module SortingNetwork (
  input  [7:0] in_1,
  input  [7:0] in_2,
  input  [7:0] in_3,
  input  [7:0] in_4,
  input  [7:0] in_5,
  input  [7:0] in_6,
  input  [7:0] in_7,
  input  [7:0] in_8,
  output [7:0] out_9,
  output [7:0] out_10,
  output [7:0] out_11,
  output [7:0] out_12,
  output [7:0] out_13,
  output [7:0] out_14,
  output [7:0] out_15,
  output [7:0] out_16,
  output Iguales
);

  EightnumberSort eightnumbersort_1 (
    .in_1(in_1), .in_2(in_2), .in_3(in_3), .in_4(in_4), .in_5(in_5), .in_6(in_6), .in_7(in_7), .in_8(in_8),
    .De_menor(out_9), .out_10(out_10), .out_11(out_11), .out_12(out_12), .out_13(out_13), .out_14(out_14),
    .out_15(out_15), .A_mayor(out_16), .Igual(Iguales));
  // Probe on out_9
  // Probe on out_10
  // Probe on out_11
  // Probe on out_12
  // Probe on out_13
  // Probe on out_14
  // Probe on out_15
  // Probe on out_16
endmodule
